# Fritzing sketch Arduino Kart (saved by Fritzing 0.9.9b)
circuit board: 8.46667cm x 5.64444cm
breadboards: 1

parts:
  M3 = DC Motor
  M4 = DC Motor
  Part1 = Arduino Uno (Rev3)
  VCC1 = Battery block 9V
  S1 = Round Pushbutton
  TCRT1 = TCRT5000 digital module [part_number=151608]
  TCRT2 = TCRT5000 digital module [part_number=151608]
  TCRT3 = TCRT5000 digital module [part_number=151608]
  TCRT4 = TCRT5000 digital module [part_number=151608]
  R1 = Resistor [tolerance=±5% power=0.25 resistance=220 package=THT]
  S2 = Pushbutton [package="[THT]"]
  Mod1 = L298N DC motor driver

nets:
  N1: M3.pin_1, Mod1.OUT4
  N2: M3.pin_2, Mod1.OUT3
  N3: M4.pin_1, Mod1.OUT2
  N4: M4.pin_2, Mod1.OUT1
  N5: Part1.D8, TCRT4.DO1
  N6: Part1.D9_PWM, Mod1.IN2
  N7: Part1.D10_PWM/SS, Mod1.IN1
  N8: Part1.D11_PWM/MOSI, Mod1.ENA
  N9: Part1.D13/SCK, R1.Pin_1, S2.Pin_3, S2.Pin_4
  N10: Part1.D2, TCRT1.DO1
  N11: Part1.D3_PWM, Mod1.ENB
  N12: Part1.D4, TCRT2.DO1
  N13: Part1.D5_PWM, Mod1.IN4
  N14: Part1.D6_PWM, Mod1.IN3
  N15: Part1.D7, TCRT3.DO1
  N16: Part1.3V3, S2.Pin_1, S2.Pin_2
  VCC: Part1.5V, TCRT1.VCC, TCRT2.VCC, TCRT3.VCC, TCRT4.VCC, Mod1.5V, Mod1.+5V-J2
  GND: Part1.GND, VCC1.-, TCRT1.GND, TCRT2.GND, TCRT3.GND, TCRT4.GND, R1.Pin_0, Mod1.GND
  N17: VCC1.+, S1.leg0
  N18: S1.leg1, Mod1.12V, Mod1.5V-ENA-JMP-O

notes:
  右电机
  左电机
  1
  2
  3
  4

custom parts:
  TCRT5000 digital module: breakout board for TCRT5000 module, convert analog to digital - Uses TCRT5000 infrared reflectance sensor - Detection distance: 1mm~8mm - Focus distance: 2.5mm - Working voltage: 3.3V~12V - Uses wide voltage LM393 comparator - With multi-turn precision potentiometer to adjust the sensitivity - Current: > 15mA - Output type: Digital switch output (0, 1) - Suitable for watt-hour meter pulse data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
  L298N DC motor driver: 2x DC motor driver with 78M05 positive voltage regulator (7..35 V) L298N: max 46 V, 2 A Set 5 V Enable jumper to enable 5 V regultor (needed for the L298N) and +5 V output at screw terminal or supply external +5 V at screw terminal Set ENA and/or ENB to +5 V to enable motor permanently or supply ENA and/or ENB with PWM signal IN1 and IN2 set rotation directory for motor A (OUT1/OUT2) IN2 and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
